# Fritzing sketch esquema_montaje (saved by Fritzing 1.0.1rc)

parts:
  Componente2 = iceZUM Alhambra
  S1 = 0.91 inch OLED I2C Display 128 x 32 Pixels
  J1 = Piezo Speaker
  M2 = Dagu DGServo 9g (Pan and tilt) [part_number=RS001B]
  Componente3 = Arduino Uno (Rev3)

nets:
  N1: Componente2.D3, Componente2.V3#56, M2.pulse
  N2: Componente2.D5, Componente2.V5, Componente3.D7
  N3: Componente2.G3, M2.gnd
  N4: Componente2.G2, J1.pin1
  N5: Componente2.V6, Componente2.V3#42, Componente2.V2, J1.pin2, M2.vcc
  VCC: S1.VCC, Componente3.5V
  GND: S1.GND, Componente3.GND
  N6: S1.SDA, Componente3.A4/SDA
  N7: S1.SCL, Componente3.A5/SCL

custom parts:
  iceZUM Alhambra: Arduino/zum compatible Open FPGA electronic board. Synthesize hardware easily, using only open source tools
